# Fritzing sketch wireless_gyro_fritzing (saved by Fritzing 0.9.2b)
breadboards: 1

parts:
  Part1 = Arduino Leonardo (Rev3b)
  Part2 = Arduino Uno (Rev3)
  GY1 = MPU-6050 Board GY-521 [form="♀ (female)" package=THT]
  NRF24L1 = NRF24L01
  NRF24L2 = NRF24L01

nets:
  N1: Part1.D2/SDA, NRF24L2.IRQ
  3V3: Part1.3V3, NRF24L2.VCC
  N2: Part1.D9_PWM/A9, NRF24L2.CE
  N3: Part1.D10_PWM/A10, NRF24L2.CSN
  N4: Part1.D11_PWM, NRF24L2.MOSI
  N5: Part1.D12/A11, NRF24L2.MISO
  N6: Part1.D13_PWM, NRF24L2.SCK
  GND: Part1.GND, NRF24L2.GND
  N7: Part2.A4/SDA, GY1.pin4
  N8: Part2.A5/SCL, GY1.pin3
  N9: Part2.D9_PWM, NRF24L1.CE
  N10: Part2.D10_PWM/SS, NRF24L1.CSN
  N11: Part2.D11_PWM/MOSI, NRF24L1.MOSI
  N12: Part2.D12/MISO, NRF24L1.MISO
  N13: Part2.D13/SCK, NRF24L1.SCK
  GND_2: Part2.GND, GY1.pin2, NRF24L1.GND
  N14: Part2.D2, NRF24L1.IRQ
  3V3_2: Part2.3V3, NRF24L1.VCC
  N15: Part2.5V, GY1.pin1

custom parts:
  MPU-6050 Board GY-521: Acelerometro y Giroscopio MPU-6050 Board GY-521
  NRF24L01: NRF24L01 module
